# Fritzing sketch Traffic Light Layout (saved by Fritzing 0.9.3b)
breadboards: 1

parts:
  Part1 = Arduino Uno (Rev3) - ICSP
  R1 = Resistor [tolerance=±5% resistance=220 package=THT]
  LED1 = LED - 5mm [color="Green (555nm)" package="5 mm [THT]"]
  R2 = Resistor [tolerance=±5% resistance=220 package=THT]
  LED2 = LED - 5mm [color="Yellow (595nm)" package="5 mm [THT]"]
  LED3 = LED - 5mm [color="Red (633nm)" package="5 mm [THT]"]
  R3 = Resistor [tolerance=±5% resistance=220 package=THT]

nets:
  N1: Part1.D8, R1.Pin_0
  N2: Part1.D9_PWM, R2.Pin_0
  N3: Part1.D10_PWM/SS, R3.Pin_0
  N4: Part1.GND, LED1.anode, LED2.anode, LED3.anode
  N5: R1.Pin_1, LED1.cathode
  N6: R2.Pin_1, LED2.cathode
  N7: LED3.cathode, R3.Pin_1
