# Fritzing sketch Robotic Arm (saved by Fritzing 0.9.3b)
breadboards: 1

parts:
  U1 = POT [package=pot_alpha_rv16af-20]
  Part1 = Arduino Uno (Rev3)
  J1 = Basic Servo

nets:
  5V: U1.A, Part1.5V, J1.vcc
  N1: U1.S, Part1.A0
  GND: U1.E, Part1.GND, J1.gnd
  N2: Part1.D9_PWM, J1.pulse
