# Fritzing sketch Train Crossing (saved by Fritzing 0.9.3b)
breadboards: 1

parts:
  U1 = POT [package=pot_alpha_rv16af-20]
  Part1 = Arduino Uno (Rev3)
  J1 = Basic Servo
  LED1 = smd LED [color="Red (633nm)" package="0805 [SMD]"]
  LED2 = smd LED [color="Green (555nm)" package="0805 [SMD]"]

nets:
  5V: U1.A, Part1.5V, J1.vcc
  N1: U1.S, Part1.A0
  GND: U1.E, Part1.GND, J1.gnd, LED1.cathode, LED2.cathode
  N2: Part1.D9_PWM, J1.pulse
  N3: Part1.D6_PWM, LED1.anode
  N4: Part1.D7, LED2.anode
